# Fritzing sketch Detector (saved by Fritzing 0.9.3b)

parts:
  Part1 = Arduino Leonardo (Rev3b)
  Part2 = Adafruit 1.44 inch TFT Breakout [part_number="Adafruit #2088"]
  LED1 = RGB LED - (4 legs) [package="5 mm [THT]"]
  Part3 = Adafruit MAX31865 RTD Sensor Breakout [part_number="Adafruit #3328"]
  U3 = IC, SIP package, 3 pins [chip_label=PT1000]
  R1 = Resistor [tolerance=±5% resistance=560 package="0603 [SMD]"]
  R2 = Resistor [tolerance=±5% resistance=560 package="0603 [SMD]"]
  R3 = Resistor [tolerance=±5% resistance=560 package="0603 [SMD]"]

nets:
  N1: Part1.D2/SDA, Part1.SDA, Part3.CS
  N2: Part1.D3_PWM/SCL, Part1.SCL, Part3.SDI
  N3: Part1.D4/A6, Part3.SDO
  N4: Part1.D5_PWM, Part3.SCLK
  N5: Part1.D6_PWM/A7, Part2.MOSI
  N6: Part1.D7, Part2.SCK
  VIN: Part1.5V, Part2.VIN, LED1.common_anode, Part3.VIN
  GND: Part1.GND, Part2.GND, Part3.GND
  N7: Part1.A0, R3.Pin_0
  N8: Part1.A1, R2.Pin_0
  N9: Part1.A2, R1.Pin_0
  N10: Part1.D8/A8, Part2.TFTCS
  N11: Part1.D9_PWM/A9, Part2.RESET
  N12: Part1.D10_PWM/A10, Part2.TFTDC
  N13: LED1.red_cathode, R3.Pin_1
  N14: LED1.green_cathode, R2.Pin_1
  N15: LED1.blue_cathode, R1.Pin_1
  N16: Part3.RTDIN+, U3.pin3
  N17: Part3.FORCE-, U3.pin1
  N18: Part3.RTDIN-, U3.pin2

custom parts:
  Adafruit 1.44 inch TFT Breakout: This lovely little display breakout is the best way to add a small, colorful and bright display to any project. Since the display uses 4-wire SPI to communicate and has its own pixel-addressable frame buffer, it can be used with every kind of microcontroller. Even a very small one with low memory and few pins available! The 1.44" display has 128x128 color pixels. Unlike the low cost "Nokia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
  Adafruit MAX31865 RTD Sensor Breakout: For precision temperature sensing, nothing beats a Platinum RTD. Resistance temperature detectors (RTDs) are temperature sensors that contain a resistor that changes resistance value as its temperature changes, basically a kind of thermistor. In this sensor, the resistor is actually a small strip of Platinum with a resistance of 100 ohms at 0°C, thus the name PT100. Compared to most NTC/PTC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
