# Fritzing sketch MissionPossibleIR (saved by Fritzing 0.9.3b)

parts:
  U1 = atmega328 [package=dip]
  IR_Reciever = IC, DIP package, 4 pins [chip_label=IRR]
  IR_Transmitter = IC, DIP package, 4 pins [chip_label=IRT]
  AAA1 = Battery Holders [package=battery-aa]
  AAA2 = Battery Holders [package=battery-aa]
  AAA3 = Battery Holders [package=battery-aa]
  Y1 = Resonator [frequency="16 Mhz" package=THT]
  DC_Motor = DC Motor
  Q1 = NPN-Transistor [package="TO92 [THT]"]
  R1 = Resistor [tolerance=±5% resistance=220 package="1206 [SMD]"]
  D1 = Schottky Diode [part_number=1N5817 package="300 mil [THT]"]
  R2 = Resistor [tolerance=±5% resistance=220 package="1206 [SMD]"]

nets:
  N1: U1.RESET, R2.Pin_0
  N2: U1.D2, IR_Reciever.pin4
  N3: U1.D3_(PWM), R1.Pin_1
  N4: U1.VCC, U1.AVCC, IR_Reciever.pin2, IR_Transmitter.pin2, AAA1.+, DC_Motor.pin_1, D1.cathode, R2.Pin_1
  GND: U1.GND, IR_Reciever.pin1, IR_Transmitter.pin1, AAA3.-, Y1.GND, Q1.C
  N5: U1.XLAT1, Y1.0
  N6: U1.XLAT2, Y1.pin_1
  N7: AAA1.-, AAA2.+
  N8: AAA2.-, AAA3.+
  N9: DC_Motor.pin_2, Q1.E, D1.anode
  N10: Q1.B, R1.Pin_0
